# Fritzing sketch PULSE SENSOR (saved by Fritzing 0.9.3b)
circuit board: 5.32982cm x 3.46548cm
breadboards: 1

parts:
  ADC1 = MCP3008 [package=dil16]
  Raspberry_Pi1 = Raspberry Pi B+

nets:
  N1: ADC1.DGND, ADC1.AGND, Raspberry_Pi1.GND
  N2: ADC1.CS/SHDN, Raspberry_Pi1.GPIO8
  N3: ADC1.Din, Raspberry_Pi1.GPIO10
  N4: ADC1.Dout, Raspberry_Pi1.GPIO9
  N5: ADC1.CLK, Raspberry_Pi1.GPIO11
  3V3: ADC1.VREF, ADC1.VDD, Raspberry_Pi1.3v3, Raspberry_Pi1.3V3

notes:
  Baltej Bal
  MCP3008
  Data Cable
